// Logisim project DiepTuanTu_DH05251531.circ as structural Verilog
module cau1 (
);

  wire clock_1_out, clock_2_out, d_ff_1_q, d_ff_2_q, d_ff_3_q, d_ff_3_qn, d_ff_5_q, d_ff_5_qn, n7474_1_pin1,
       n7474_1_pin2, n7474_1_pin5, n7474_1_pin9, n7474_2_pin5, n7474_2_pin9;

  Clock clock_1 (.out(clock_1_out));
  Clock clock_2 (.out(clock_2_out));
  D_Flip_Flop d_ff_1 (.D(d_ff_5_qn), .clk(clock_2_out), .Q(d_ff_1_q), .preset(1'b0), .reset(1'b0));  // open: Qn
  _7474 #(.ShowInternalStructure("true")) u_7474_1 (
    .pin1(n7474_1_pin1), .pin2(n7474_1_pin2), .pin3(clock_1_out), .pin4(n7474_1_pin1), .pin5(n7474_1_pin5),
    .pin13(n7474_1_pin1), .pin12(n7474_1_pin5), .pin11(clock_1_out), .pin10(n7474_1_pin1), .pin9(n7474_1_pin9));  // open: pin6, pin8
  D_Flip_Flop d_ff_2 (.D(d_ff_1_q), .clk(clock_2_out), .Q(d_ff_2_q), .preset(1'b0), .reset(1'b0));  // open: Qn
  D_Flip_Flop d_ff_3 (.D(d_ff_2_q), .clk(clock_2_out), .Q(d_ff_3_q), .Qn(d_ff_3_qn), .preset(1'b0), .reset(1'b0));
  D_Flip_Flop d_ff_4 (.D(d_ff_2_q), .clk(clock_2_out), .Q(d_ff_3_q), .Qn(d_ff_3_qn), .preset(1'b0), .reset(1'b0));
  _7474 #(.ShowInternalStructure("true")) u_7474_2 (
    .pin1(n7474_1_pin1), .pin2(n7474_1_pin9), .pin3(clock_1_out), .pin4(n7474_1_pin1), .pin5(n7474_2_pin5),
    .pin13(n7474_1_pin1), .pin12(n7474_2_pin5), .pin11(clock_1_out), .pin10(n7474_1_pin1),
    .pin9(n7474_2_pin9), .pin8(n7474_1_pin2));  // open: pin6
  D_Flip_Flop d_ff_5 (.D(d_ff_3_q), .clk(clock_2_out), .Q(d_ff_5_q), .Qn(d_ff_5_qn), .preset(1'b0), .reset(1'b0));
  D_Flip_Flop d_ff_6 (.D(d_ff_3_q), .clk(clock_2_out), .Q(d_ff_5_q), .Qn(d_ff_5_qn), .preset(1'b0), .reset(1'b0));
  LED led_1 (.in(n7474_2_pin9));
  LED led_2 (.in(d_ff_5_q));
  // also tied to VCC on the sheet: n7474_1_pin1

  // Notes on the sheet:
  //   Clock
  //   Q3
  //   Q3
endmodule

module cau2 (
);

  wire clock_1_out, clock_2_out, d_ff_1_q, d_ff_2_q, d_ff_3_q, d_ff_3_qn, d_ff_5_q, d_ff_5_qn, n7474_1_pin1,
       n7474_1_pin2, n7474_1_pin5, n7474_1_pin9, n7474_2_pin5, n7474_2_pin9;

  Clock clock_1 (.out(clock_1_out));
  Clock clock_2 (.out(clock_2_out));
  _7474 #(.ShowInternalStructure("true")) u_7474_1 (
    .pin1(n7474_1_pin1), .pin2(n7474_1_pin2), .pin3(clock_1_out), .pin4(n7474_1_pin1), .pin5(n7474_1_pin5),
    .pin13(n7474_1_pin1), .pin12(n7474_1_pin5), .pin11(clock_1_out), .pin10(n7474_1_pin1), .pin9(n7474_1_pin9));  // open: pin6, pin8
  LED led_1 (.in(d_ff_1_q));
  D_Flip_Flop d_ff_1 (.D(d_ff_5_qn), .clk(clock_2_out), .Q(d_ff_1_q), .preset(1'b0), .reset(1'b0));  // open: Qn
  LED led_2 (.in(n7474_1_pin5));
  D_Flip_Flop d_ff_2 (.D(d_ff_1_q), .clk(clock_2_out), .Q(d_ff_2_q), .preset(1'b0), .reset(1'b0));  // open: Qn
  LED led_3 (.in(d_ff_2_q));
  D_Flip_Flop d_ff_3 (.D(d_ff_2_q), .clk(clock_2_out), .Q(d_ff_3_q), .Qn(d_ff_3_qn), .preset(1'b0), .reset(1'b0));
  D_Flip_Flop d_ff_4 (.D(d_ff_2_q), .clk(clock_2_out), .Q(d_ff_3_q), .Qn(d_ff_3_qn), .preset(1'b0), .reset(1'b0));
  LED led_4 (.in(n7474_1_pin9));
  LED led_5 (.in(d_ff_3_q));
  LED led_6 (.in(n7474_2_pin5));
  _7474 #(.ShowInternalStructure("true")) u_7474_2 (
    .pin1(n7474_1_pin1), .pin2(n7474_1_pin9), .pin3(clock_1_out), .pin4(n7474_1_pin1), .pin5(n7474_2_pin5),
    .pin13(n7474_1_pin1), .pin12(n7474_2_pin5), .pin11(clock_1_out), .pin10(n7474_1_pin1),
    .pin9(n7474_2_pin9), .pin8(n7474_1_pin2));  // open: pin6
  LED led_7 (.in(d_ff_5_q));
  D_Flip_Flop d_ff_5 (.D(d_ff_3_q), .clk(clock_2_out), .Q(d_ff_5_q), .Qn(d_ff_5_qn), .preset(1'b0), .reset(1'b0));
  D_Flip_Flop d_ff_6 (.D(d_ff_3_q), .clk(clock_2_out), .Q(d_ff_5_q), .Qn(d_ff_5_qn), .preset(1'b0), .reset(1'b0));
  LED led_8 (.in(n7474_2_pin9));
  // also tied to VCC on the sheet: n7474_1_pin1

  // Notes on the sheet:
  //   Clock
  //   Q0
  //   Q0
  //   Q1
  //   Q1
  //   Q2
  //   Q2
  //   Q3
  //   Q3
endmodule

module cau3 (
);

  wire clock_1_out, j_k_ff_1_q, j_k_ff_1_qn, j_k_ff_2_q, j_k_ff_2_qn, j_k_ff_3_q, j_k_ff_3_qn, j_k_ff_4_q,
       j_k_ff_4_qn;

  Clock clock_1 (.out(clock_1_out));
  J_K_Flip_Flop j_k_ff_1 (
    .J(j_k_ff_4_qn), .K(j_k_ff_4_q), .clk(clock_1_out), .Q(j_k_ff_1_q), .Qn(j_k_ff_1_qn), .preset(1'b0),
    .reset(1'b0));
  LED led_1 (.in(j_k_ff_1_q));
  J_K_Flip_Flop j_k_ff_2 (
    .J(j_k_ff_1_q), .K(j_k_ff_1_qn), .clk(clock_1_out), .Q(j_k_ff_2_q), .Qn(j_k_ff_2_qn), .preset(1'b0),
    .reset(1'b0));
  LED led_2 (.in(j_k_ff_2_q));
  J_K_Flip_Flop j_k_ff_3 (
    .J(j_k_ff_2_q), .K(j_k_ff_2_qn), .clk(clock_1_out), .Q(j_k_ff_3_q), .Qn(j_k_ff_3_qn), .preset(1'b0),
    .reset(1'b0));
  LED led_3 (.in(j_k_ff_3_q));
  J_K_Flip_Flop j_k_ff_4 (
    .J(j_k_ff_3_q), .K(j_k_ff_3_qn), .clk(clock_1_out), .Q(j_k_ff_4_q), .Qn(j_k_ff_4_qn), .preset(1'b0),
    .reset(1'b0));
  LED led_4 (.in(j_k_ff_4_q));

  // Notes on the sheet:
  //   Clock
  //   Q0
  //   Q1
  //   Q2
  //   Q3
endmodule

module cau4 (
  input  Load,
  input  [3:0] in_2,
  input  Load_2,
  input  [3:0] in_4
);

  wire and_1_out, and_2_out, and_3_out, and_4_out, and_5_out, and_6_out, and_7_out, and_8_out, clock_1_out,
       d_ff_1_q, d_ff_2_q, d_ff_3_q, d_ff_4_q, d_ff_4_qn, n7408_1_pin1, n7408_1_pin2, n7408_1_pin3,
       n7408_1_pin6, n7408_1_pin8, n7408_1_pin9, n7408_1_pin11, n7408_2_pin1, n7408_2_pin3, n7408_2_pin6,
       n7408_2_pin8, n7408_2_pin9, n7408_2_pin11, n7432_1_pin3, n7432_1_pin6, n7432_1_pin8, n7432_1_pin11,
       n7474_1_pin1, n7474_1_pin3, n7474_2_pin9, not_2_out, or_1_out, or_2_out, or_3_out, or_4_out;

  _7408 #(.ShowInternalStructure("true")) u_7408_1 (
    .pin1(n7408_1_pin1), .pin2(n7408_1_pin2), .pin3(n7408_1_pin3), .pin4(in_4[0]), .pin5(Load_2),
    .pin6(n7408_1_pin6), .pin13(Load_2), .pin12(in_4[1]), .pin11(n7408_1_pin11), .pin10(n7408_1_pin2),
    .pin9(n7408_1_pin9), .pin8(n7408_1_pin8));
  not not_1 (n7408_1_pin2, Load_2);
  Clock clock_1 (.out(clock_1_out));
  not not_2 (not_2_out, Load);
  _7408 #(.ShowInternalStructure("true")) u_7408_2 (
    .pin1(n7408_2_pin1), .pin2(n7408_1_pin2), .pin3(n7408_2_pin3), .pin4(in_4[2]), .pin5(Load_2),
    .pin6(n7408_2_pin6), .pin13(Load_2), .pin12(in_4[3]), .pin11(n7408_2_pin11), .pin10(n7408_1_pin2),
    .pin9(n7408_2_pin9), .pin8(n7408_2_pin8));
  and and_1 (and_1_out, d_ff_4_qn, not_2_out);
  and and_2 (and_2_out, in_2[0], Load);
  and and_3 (and_3_out, d_ff_1_q, not_2_out);
  and and_4 (and_4_out, in_2[1], Load);
  and and_5 (and_5_out, d_ff_2_q, not_2_out);
  and and_6 (and_6_out, in_2[2], Load);
  and and_7 (and_7_out, d_ff_3_q, not_2_out);
  and and_8 (and_8_out, in_2[3], Load);
  or or_1 (or_1_out, and_1_out, and_2_out);
  or or_2 (or_2_out, and_3_out, and_4_out);
  or or_3 (or_3_out, and_5_out, and_6_out);
  or or_4 (or_4_out, and_7_out, and_8_out);
  _7432 #(.ShowInternalStructure("true")) u_7432_1 (
    .pin1(n7408_1_pin3), .pin2(n7408_1_pin6), .pin3(n7432_1_pin3), .pin4(n7408_1_pin8), .pin5(n7408_1_pin11),
    .pin6(n7432_1_pin6), .pin13(n7408_2_pin11), .pin12(n7408_2_pin8), .pin11(n7432_1_pin11),
    .pin10(n7408_2_pin6), .pin9(n7408_2_pin3), .pin8(n7432_1_pin8));
  D_Flip_Flop d_ff_1 (.D(or_1_out), .clk(clock_1_out), .Q(d_ff_1_q), .preset(1'b0), .reset(1'b0));  // open: Qn
  D_Flip_Flop d_ff_2 (.D(or_2_out), .clk(clock_1_out), .Q(d_ff_2_q), .preset(1'b0), .reset(1'b0));  // open: Qn
  D_Flip_Flop d_ff_3 (.D(or_3_out), .clk(clock_1_out), .Q(d_ff_3_q), .preset(1'b0), .reset(1'b0));  // open: Qn
  D_Flip_Flop d_ff_4 (.D(or_4_out), .clk(clock_1_out), .Q(d_ff_4_q), .Qn(d_ff_4_qn), .preset(1'b0), .reset(1'b0));
  LED led_1 (.in(d_ff_4_q));
  _7474 #(.ShowInternalStructure("true")) u_7474_1 (
    .pin1(n7474_1_pin1), .pin2(n7432_1_pin3), .pin3(n7474_1_pin3), .pin4(n7474_1_pin1), .pin5(n7408_1_pin9),
    .pin13(n7474_1_pin1), .pin12(n7432_1_pin6), .pin11(n7474_1_pin3), .pin10(n7474_1_pin1),
    .pin9(n7408_2_pin1));  // open: pin6, pin8
  Clock clock_2 (.out(n7474_1_pin3));
  _7474 #(.ShowInternalStructure("true")) u_7474_2 (
    .pin1(n7474_1_pin1), .pin2(n7432_1_pin8), .pin3(n7474_1_pin3), .pin4(n7474_1_pin1), .pin5(n7408_2_pin9),
    .pin13(n7474_1_pin1), .pin12(n7432_1_pin11), .pin11(n7474_1_pin3), .pin10(n7474_1_pin1),
    .pin9(n7474_2_pin9), .pin8(n7408_1_pin1));  // open: pin6
  LED led_2 (.in(n7474_2_pin9));
  // also tied to VCC on the sheet: n7474_1_pin1

  // Notes on the sheet:
  //   Data in
  //   Data in
  //   Clock
  //   Q3
  //   Q3
endmodule

module cau5 (
  input  Load,
  input  [3:0] in_2,
  input  Load_2,
  input  [3:0] in_4
);

  wire and_1_out, and_2_out, and_3_out, and_4_out, and_5_out, and_6_out, and_7_out, and_8_out, clock_1_out,
       d_ff_1_q, d_ff_2_q, d_ff_3_q, d_ff_4_q, d_ff_4_qn, n7408_1_pin1, n7408_1_pin2, n7408_1_pin3,
       n7408_1_pin6, n7408_1_pin8, n7408_1_pin9, n7408_1_pin11, n7408_2_pin1, n7408_2_pin3, n7408_2_pin6,
       n7408_2_pin8, n7408_2_pin9, n7408_2_pin11, n7432_1_pin3, n7432_1_pin6, n7432_1_pin8, n7432_1_pin11,
       n7474_1_pin1, n7474_1_pin3, n7474_2_pin9, not_2_out, or_1_out, or_2_out, or_3_out, or_4_out;

  _7408 #(.ShowInternalStructure("true")) u_7408_1 (
    .pin1(n7408_1_pin1), .pin2(n7408_1_pin2), .pin3(n7408_1_pin3), .pin4(in_4[0]), .pin5(Load_2),
    .pin6(n7408_1_pin6), .pin13(Load_2), .pin12(in_4[1]), .pin11(n7408_1_pin11), .pin10(n7408_1_pin2),
    .pin9(n7408_1_pin9), .pin8(n7408_1_pin8));
  not not_1 (n7408_1_pin2, Load_2);
  Clock clock_1 (.out(clock_1_out));
  not not_2 (not_2_out, Load);
  _7408 #(.ShowInternalStructure("true")) u_7408_2 (
    .pin1(n7408_2_pin1), .pin2(n7408_1_pin2), .pin3(n7408_2_pin3), .pin4(in_4[2]), .pin5(Load_2),
    .pin6(n7408_2_pin6), .pin13(Load_2), .pin12(in_4[3]), .pin11(n7408_2_pin11), .pin10(n7408_1_pin2),
    .pin9(n7408_2_pin9), .pin8(n7408_2_pin8));
  and and_1 (and_1_out, d_ff_4_qn, not_2_out);
  and and_2 (and_2_out, in_2[0], Load);
  and and_3 (and_3_out, d_ff_1_q, not_2_out);
  and and_4 (and_4_out, in_2[1], Load);
  and and_5 (and_5_out, d_ff_2_q, not_2_out);
  and and_6 (and_6_out, in_2[2], Load);
  and and_7 (and_7_out, d_ff_3_q, not_2_out);
  and and_8 (and_8_out, in_2[3], Load);
  or or_1 (or_1_out, and_1_out, and_2_out);
  or or_2 (or_2_out, and_3_out, and_4_out);
  or or_3 (or_3_out, and_5_out, and_6_out);
  or or_4 (or_4_out, and_7_out, and_8_out);
  _7432 #(.ShowInternalStructure("true")) u_7432_1 (
    .pin1(n7408_1_pin3), .pin2(n7408_1_pin6), .pin3(n7432_1_pin3), .pin4(n7408_1_pin8), .pin5(n7408_1_pin11),
    .pin6(n7432_1_pin6), .pin13(n7408_2_pin11), .pin12(n7408_2_pin8), .pin11(n7432_1_pin11),
    .pin10(n7408_2_pin6), .pin9(n7408_2_pin3), .pin8(n7432_1_pin8));
  D_Flip_Flop d_ff_1 (.D(or_1_out), .clk(clock_1_out), .Q(d_ff_1_q), .preset(1'b0), .reset(1'b0));  // open: Qn
  D_Flip_Flop d_ff_2 (.D(or_2_out), .clk(clock_1_out), .Q(d_ff_2_q), .preset(1'b0), .reset(1'b0));  // open: Qn
  D_Flip_Flop d_ff_3 (.D(or_3_out), .clk(clock_1_out), .Q(d_ff_3_q), .preset(1'b0), .reset(1'b0));  // open: Qn
  D_Flip_Flop d_ff_4 (.D(or_4_out), .clk(clock_1_out), .Q(d_ff_4_q), .Qn(d_ff_4_qn), .preset(1'b0), .reset(1'b0));
  LED led_1 (.in(d_ff_1_q));
  LED led_2 (.in(d_ff_2_q));
  LED led_3 (.in(d_ff_3_q));
  LED led_4 (.in(d_ff_4_q));
  _7474 #(.ShowInternalStructure("true")) u_7474_1 (
    .pin1(n7474_1_pin1), .pin2(n7432_1_pin3), .pin3(n7474_1_pin3), .pin4(n7474_1_pin1), .pin5(n7408_1_pin9),
    .pin13(n7474_1_pin1), .pin12(n7432_1_pin6), .pin11(n7474_1_pin3), .pin10(n7474_1_pin1),
    .pin9(n7408_2_pin1));  // open: pin6, pin8
  Clock clock_2 (.out(n7474_1_pin3));
  LED led_5 (.in(n7408_1_pin9));
  LED led_6 (.in(n7408_2_pin1));
  _7474 #(.ShowInternalStructure("true")) u_7474_2 (
    .pin1(n7474_1_pin1), .pin2(n7432_1_pin8), .pin3(n7474_1_pin3), .pin4(n7474_1_pin1), .pin5(n7408_2_pin9),
    .pin13(n7474_1_pin1), .pin12(n7432_1_pin11), .pin11(n7474_1_pin3), .pin10(n7474_1_pin1),
    .pin9(n7474_2_pin9), .pin8(n7408_1_pin1));  // open: pin6
  LED led_7 (.in(n7408_2_pin9));
  LED led_8 (.in(n7474_2_pin9));
  // also tied to VCC on the sheet: n7474_1_pin1

  // Notes on the sheet:
  //   Data in
  //   Data in
  //   Clock
  //   Q0
  //   Q1
  //   Q2
  //   Q3
  //   Q0
  //   Q1
  //   Q2
  //   Q3
endmodule

module cau6 (
  input  Clear
);

  wire clock_1_out, n7474_1_pin2, n7474_1_pin5, n7474_1_pin7, n7474_1_pin9, n7474_1_pin14, n7474_2_pin5,
       n7474_2_pin7, n7474_2_pin9, n7474_2_pin14, n7474_3_pin5, n7474_3_pin7, n7474_3_pin9, n7474_3_pin14,
       n7474_4_pin5, n7474_4_pin7, n7474_4_pin9, n7474_4_pin14;

  Clock clock_1 (.out(clock_1_out));
  _7474 #(.ShowInternalStructure("true"), .VccGndPorts("true")) u_7474_1 (
    .pin1(Clear), .pin2(n7474_1_pin2), .pin3(clock_1_out), .pin5(n7474_1_pin5), .pin7(n7474_1_pin7),
    .pin14(n7474_1_pin14), .pin13(Clear), .pin12(n7474_1_pin5), .pin11(clock_1_out), .pin9(n7474_1_pin9));  // open: pin4, pin6, pin10, pin8
  LED led_1 (.in(n7474_1_pin5));
  LED led_2 (.in(n7474_1_pin9));
  LED led_3 (.in(n7474_2_pin5));
  _7474 #(.ShowInternalStructure("true"), .VccGndPorts("true")) u_7474_2 (
    .pin1(Clear), .pin2(n7474_1_pin9), .pin3(clock_1_out), .pin5(n7474_2_pin5), .pin7(n7474_2_pin7),
    .pin14(n7474_2_pin14), .pin13(Clear), .pin12(n7474_2_pin5), .pin11(clock_1_out), .pin9(n7474_2_pin9));  // open: pin4, pin6, pin10, pin8
  LED led_4 (.in(n7474_2_pin9));
  LED led_5 (.in(n7474_3_pin5));
  LED led_6 (.in(n7474_3_pin9));
  LED led_7 (.in(n7474_4_pin5));
  LED led_8 (.in(n7474_4_pin9));
  LED led_9 (.in(n7474_4_pin9));
  LED led_10 (.in(n7474_4_pin5));
  LED led_11 (.in(n7474_3_pin9));
  LED led_12 (.in(n7474_2_pin5));
  LED led_13 (.in(n7474_1_pin9));
  LED led_14 (.in(n7474_3_pin5));
  LED led_15 (.in(n7474_2_pin9));
  _7474 #(.ShowInternalStructure("true"), .VccGndPorts("true")) u_7474_3 (
    .pin1(Clear), .pin2(n7474_2_pin9), .pin3(clock_1_out), .pin5(n7474_3_pin5), .pin7(n7474_3_pin7),
    .pin14(n7474_3_pin14), .pin13(Clear), .pin12(n7474_3_pin5), .pin11(clock_1_out), .pin9(n7474_3_pin9));  // open: pin4, pin6, pin10, pin8
  LED led_16 (.in(n7474_1_pin5));
  _7474 #(.ShowInternalStructure("true"), .VccGndPorts("true")) u_7474_4 (
    .pin1(Clear), .pin2(n7474_3_pin9), .pin3(clock_1_out), .pin5(n7474_4_pin5), .pin7(n7474_4_pin7),
    .pin14(n7474_4_pin14), .pin13(Clear), .pin12(n7474_4_pin5), .pin11(clock_1_out), .pin9(n7474_4_pin9),
    .pin8(n7474_1_pin2));  // open: pin4, pin6, pin10
  // also tied to GND on the sheet: {n7474_1_pin7, n7474_2_pin7, n7474_3_pin7, n7474_4_pin7}
  // also tied to VCC on the sheet: {n7474_1_pin14, n7474_2_pin14, n7474_3_pin14, n7474_4_pin14}

  // Notes on the sheet:
  //   Clock
endmodule
